// Logisim project cpu.circ as structural Verilog: 7 circuits, main circuit main
module main (
  input  Reset,
  output [31:0] out_2,
  output out_3,
  output [4:0] out_4,
  output [31:0] out_5,
  output out_6,
  output [4:0] out_7,
  output [31:0] out_8
);

  wire alu_1_zero, and_1_out, clock_1_out, controller_1_alusrc, controller_1_npc_sel, controller_1_regdst,
       Mem2Reg;
  wire [1:0] controller_1_aluctr, controller_1_extop;
  wire [4:0] splitter_1_rd, splitter_1_rs, splitter_1_rt;
  wire [5:0] splitter_1_func, splitter_1_op;
  wire [15:0] splitter_1_immediate;
  wire [31:0] adder_1_out, adder_2_out, alu_1_out, ext_1_out_3, grf_1_rd1, ifu_1_out_5, multiplexer_3_out,
       multiplexer_4_out, ram_1_data, shifter_1_out;

  Clock clock_1 (.out(clock_1_out));
  IFU ifu_1 (.in_2(multiplexer_4_out), .in_3(Reset), .in_1(clock_1_out), .Instr(out_2), .out_5(ifu_1_out_5));
  Splitter splitter_1 (
    .Instr(out_2), .func(splitter_1_func), .immediate(splitter_1_immediate), .Rd(splitter_1_rd),
    .Rt(splitter_1_rt), .Rs(splitter_1_rs), .op(splitter_1_op));
  Controller controller_1 (
    .op(splitter_1_op), .func(splitter_1_func), .RegDst(controller_1_regdst), .ALUSrc(controller_1_alusrc),
    .MemtoReg(Mem2Reg), .RegWrite(out_3), .MemWrite(out_6), .nPC_Sel(controller_1_npc_sel),
    .ExtOp(controller_1_extop), .ALUctr(controller_1_aluctr));
  Multiplexer #(.width(5), .disabled(0)) multiplexer_1 (
    .in0(splitter_1_rt), .in1(splitter_1_rd), .out(out_4), .sel(controller_1_regdst));  // open: en
  // Probe on splitter_1_rs
  // Probe on splitter_1_rt
  GRF grf_1 (
    .RA1(splitter_1_rs), .RA2(splitter_1_rt), .WA_A3(out_4), .WD(out_5), .clk(clock_1_out), .RegWrite(out_3),
    .RD1(grf_1_rd1), .RD2(out_8));
  EXT ext_1 (.in_2(splitter_1_immediate), .Extop(controller_1_extop), .out_3(ext_1_out_3));
  Multiplexer #(.width(32), .disabled(0)) multiplexer_2 (
    .in0({alu_1_out[31:7], out_7, alu_1_out[1:0]}), .in1(ram_1_data), .out(out_5), .sel(Mem2Reg));  // open: en
  Shifter #(.width(32)) shifter_1 (.in(ext_1_out_3), .\dist (5'b00010), .out(shifter_1_out));
  Multiplexer #(.width(32), .disabled(0)) multiplexer_3 (
    .in0(out_8), .in1(ext_1_out_3), .out(multiplexer_3_out), .sel(controller_1_alusrc));  // open: en
  Adder #(.width(32)) adder_1 (.a(ifu_1_out_5), .b(32'h4), .out(adder_1_out));  // open: cin, cout
  ALU alu_1 (
    .A(grf_1_rd1), .B(multiplexer_3_out), .ALUOp(controller_1_aluctr),
    .Out({alu_1_out[31:7], out_7, alu_1_out[1:0]}), .zero(alu_1_zero));
  and and_1 (and_1_out, controller_1_npc_sel, alu_1_zero);
  Adder #(.width(32)) adder_2 (.a(adder_1_out), .b(shifter_1_out), .out(adder_2_out));  // open: cin, cout
  Multiplexer #(.width(32), .disabled(0)) multiplexer_4 (
    .in0(adder_1_out), .in1(adder_2_out), .out(multiplexer_4_out), .sel(and_1_out));  // open: en
  RAM #(.addrWidth(5), .dataWidth(32), .bus("separate")) ram_1 (
    .addr(out_7), .din(out_8), .data(ram_1_data), .str(out_6), .clk(clock_1_out));  // open: sel, ld, clr

  // Other names for the same wires on the sheet: Instr[31:0] = out_2; MemAddr[4:0] = out_7; MemData[31:0] = out_8;
  //   MemWrite = out_6; RegAddr[4:0] = out_4; RegData[31:0] = out_5; RegWrite = out_3
endmodule

module Controller (
  input  [5:0] op,
  input  [5:0] func,
  output RegDst,
  output ALUSrc,
  output MemtoReg,
  output RegWrite,
  output MemWrite,
  output nPC_Sel,
  output [1:0] ExtOp,
  output [1:0] ALUctr
);

  wire addu, addu_2_out, addu_out, not_1_out, not_2_out, not_3_out, not_4_out, not_5_out, not_6_out,
       not_7_out, not_8_out, not_9_out, not_10_out, not_11_out, not_12_out, ori_out, subu, subu_2_out,
       subu_out;

  not not_1 (not_1_out, op[5]);
  not not_2 (not_2_out, op[4]);
  not not_3 (not_3_out, op[3]);
  not not_4 (not_4_out, op[2]);
  not not_5 (not_5_out, op[1]);
  not not_6 (not_6_out, op[0]);
  and u_addu (addu_out, not_1_out, not_2_out, not_3_out, not_4_out, not_5_out, not_6_out);
  and u_subu (subu_out, not_1_out, not_2_out, not_3_out, not_4_out, not_5_out, not_6_out);
  and ori (ori_out, not_1_out, not_2_out, op[3], op[2], not_5_out, op[0]);
  and lw (MemtoReg, op[5], not_2_out, not_3_out, not_4_out, op[1], op[0]);
  and sw (MemWrite, op[5], not_2_out, op[3], not_4_out, op[1], op[0]);
  and beq (nPC_Sel, not_1_out, not_2_out, not_3_out, op[2], not_5_out, not_6_out);
  and lui (ExtOp[1], not_1_out, not_2_out, op[3], op[2], op[1], op[0]);
  and and_1 (addu, addu_out, addu_2_out);
  and addu_2 (addu_2_out, func[5], not_8_out, not_9_out, not_10_out, not_11_out, func[0]);
  and and_2 (subu, subu_out, subu_2_out);
  and subu_2 (subu_2_out, func[5], not_8_out, not_9_out, not_10_out, func[1], func[0]);
  or u_RegDst (RegDst, subu, addu);
  or u_ALUSrc (ALUSrc, ori_out, MemWrite, ExtOp[1], MemtoReg);
  not not_7 (not_7_out, func[5]);
  not not_8 (not_8_out, func[4]);
  not not_9 (not_9_out, func[3]);
  not not_10 (not_10_out, func[2]);
  not not_11 (not_11_out, func[1]);
  not not_12 (not_12_out, func[0]);
  or u_RegWrite (RegWrite, ori_out, MemtoReg, ExtOp[1], addu, subu);
  or u_ExtOp (ExtOp[0], MemtoReg, nPC_Sel, MemWrite);
  or ALUctr0 (ALUctr[1], ori_out, ExtOp[1]);
  or ALUctr1 (ALUctr[0], subu, nPC_Sel);

  // Other names for the same wires on the sheet: ALUctr1 = ALUctr[0]; ALUctr0 = ALUctr[1]; ExtOp_t = ExtOp[0]
endmodule

module ALU (
  input  [1:0] ALUOp,
  input  [31:0] A,
  input  [31:0] B,
  output [31:0] Out,
  output zero
);

  wire [31:0] adder_1_out, or_1_out, subtractor_1_out, undriven;

  Adder #(.width(32)) adder_1 (.a(A), .b(B), .out(adder_1_out));  // open: cin, cout
  Subtractor #(.width(32)) subtractor_1 (.a(A), .b(B), .out(subtractor_1_out));  // open: bin, bout
  assign or_1_out = A | B;  // OR_Gate or_1, 32 bits wide
  Comparator #(.width(32)) comparator_1 (.a(A), .b(B), .eq(zero));  // open: gt, lt
  Multiplexer #(.select(2), .width(32)) multiplexer_1 (
    .in0(adder_1_out), .in1(subtractor_1_out), .in2(or_1_out), .in3(undriven), .out(Out), .sel(ALUOp));  // open: en
endmodule

module GRF (
  input  clk,
  input  RegWrite,
  input  [4:0] RA1,
  input  [4:0] RA2,
  input  [4:0] WA_A3,
  input  [31:0] WD,
  output [31:0] RD1,
  output [31:0] RD2
);

  wire decoder_1_out0, decoder_1_out1, decoder_1_out2, decoder_1_out3, decoder_1_out4, decoder_1_out5,
       decoder_1_out6, decoder_1_out7, decoder_1_out8, decoder_1_out9, decoder_1_out10, decoder_1_out11,
       decoder_1_out12, decoder_1_out13, decoder_1_out14, decoder_1_out15, decoder_1_out16, decoder_1_out17,
       decoder_1_out18, decoder_1_out19, decoder_1_out20, decoder_1_out21, decoder_1_out22, decoder_1_out23,
       decoder_1_out24, decoder_1_out25, decoder_1_out26, decoder_1_out27, decoder_1_out28, decoder_1_out29,
       decoder_1_out30, decoder_1_out31;
  wire [3:0] and_1_out, and_5_out, and_9_out, and_13_out, and_17_out, and_21_out, and_25_out, and_29_out;
  wire [31:0] _1, _1a, _1b, _1c, _2, _2a, _2b, _2c, _3, _3a, _3b, _3c, _4, _4a, _4b, _4c, _5, _5a, _5b, _5c,
       _6, _6a, _6b, _6c, _7, _7a, _7b, _7c, _8, _8a, _8b, _8c;

  Decoder #(.select(5)) decoder_1 (
    .out0(decoder_1_out0), .out1(decoder_1_out1), .out2(decoder_1_out2), .out3(decoder_1_out3),
    .out4(decoder_1_out4), .out5(decoder_1_out5), .out6(decoder_1_out6), .out7(decoder_1_out7),
    .out8(decoder_1_out8), .out9(decoder_1_out9), .out10(decoder_1_out10), .out11(decoder_1_out11),
    .out12(decoder_1_out12), .out13(decoder_1_out13), .out14(decoder_1_out14), .out15(decoder_1_out15),
    .out16(decoder_1_out16), .out17(decoder_1_out17), .out18(decoder_1_out18), .out19(decoder_1_out19),
    .out20(decoder_1_out20), .out21(decoder_1_out21), .out22(decoder_1_out22), .out23(decoder_1_out23),
    .out24(decoder_1_out24), .out25(decoder_1_out25), .out26(decoder_1_out26), .out27(decoder_1_out27),
    .out28(decoder_1_out28), .out29(decoder_1_out29), .out30(decoder_1_out30), .out31(decoder_1_out31),
    .sel(WA_A3));  // open: en
  and and_1 (and_1_out[0], RegWrite, decoder_1_out0);
  and and_2 (and_1_out[1], RegWrite, decoder_1_out1);
  and and_3 (and_1_out[2], RegWrite, decoder_1_out2);
  and and_4 (and_1_out[3], RegWrite, decoder_1_out3);
  and and_5 (and_5_out[0], RegWrite, decoder_1_out4);
  and and_6 (and_5_out[1], RegWrite, decoder_1_out5);
  and and_7 (and_5_out[2], RegWrite, decoder_1_out6);
  and and_8 (and_5_out[3], RegWrite, decoder_1_out7);
  and and_9 (and_9_out[0], RegWrite, decoder_1_out8);
  and and_10 (and_9_out[1], RegWrite, decoder_1_out9);
  and and_11 (and_9_out[2], RegWrite, decoder_1_out10);
  and and_12 (and_9_out[3], RegWrite, decoder_1_out11);
  and and_13 (and_13_out[0], RegWrite, decoder_1_out12);
  and and_14 (and_13_out[1], RegWrite, decoder_1_out13);
  and and_15 (and_13_out[2], RegWrite, decoder_1_out14);
  and and_16 (and_13_out[3], RegWrite, decoder_1_out15);
  and and_17 (and_17_out[0], RegWrite, decoder_1_out16);
  and and_18 (and_17_out[1], RegWrite, decoder_1_out17);
  and and_19 (and_17_out[2], RegWrite, decoder_1_out18);
  and and_20 (and_17_out[3], RegWrite, decoder_1_out19);
  and and_21 (and_21_out[0], RegWrite, decoder_1_out20);
  and and_22 (and_21_out[1], RegWrite, decoder_1_out21);
  and and_23 (and_21_out[2], RegWrite, decoder_1_out22);
  and and_24 (and_21_out[3], RegWrite, decoder_1_out23);
  and and_25 (and_25_out[0], RegWrite, decoder_1_out24);
  and and_26 (and_25_out[1], RegWrite, decoder_1_out25);
  and and_27 (and_25_out[2], RegWrite, decoder_1_out26);
  and and_28 (and_25_out[3], RegWrite, decoder_1_out27);
  and and_29 (and_29_out[0], RegWrite, decoder_1_out28);
  and and_30 (and_29_out[1], RegWrite, decoder_1_out29);
  and and_31 (and_29_out[2], RegWrite, decoder_1_out30);
  and and_32 (and_29_out[3], RegWrite, decoder_1_out31);
  Register #(.width(32)) register_1 (.en(and_1_out[0]), .Q(_1), .clk(clk));  // open: D, clr
  Register #(.width(32)) register_2 (.D(WD), .en(and_5_out[0]), .Q(_5), .clk(clk));  // open: clr
  Register #(.width(32)) register_3 (.D(WD), .en(and_9_out[0]), .Q(_1a), .clk(clk));  // open: clr
  Register #(.width(32)) register_4 (.D(WD), .en(and_13_out[0]), .Q(_5a), .clk(clk));  // open: clr
  Register #(.width(32)) register_5 (.D(WD), .en(and_17_out[0]), .Q(_1b), .clk(clk));  // open: clr
  Register #(.width(32)) register_6 (.D(WD), .en(and_21_out[0]), .Q(_5b), .clk(clk));  // open: clr
  Register #(.width(32)) register_7 (.D(WD), .en(and_25_out[0]), .Q(_1c), .clk(clk));  // open: clr
  Register #(.width(32)) register_8 (.D(WD), .en(and_29_out[0]), .Q(_5c), .clk(clk));  // open: clr
  Register #(.width(32)) register_9 (.D(WD), .en(and_1_out[1]), .Q(_2), .clk(clk));  // open: clr
  Register #(.width(32)) register_10 (.D(WD), .en(and_5_out[1]), .Q(_6), .clk(clk));  // open: clr
  Register #(.width(32)) register_11 (.D(WD), .en(and_9_out[1]), .Q(_2a), .clk(clk));  // open: clr
  Register #(.width(32)) register_12 (.D(WD), .en(and_13_out[1]), .Q(_6a), .clk(clk));  // open: clr
  Register #(.width(32)) register_13 (.D(WD), .en(and_17_out[1]), .Q(_2b), .clk(clk));  // open: clr
  Register #(.width(32)) register_14 (.D(WD), .en(and_21_out[1]), .Q(_6b), .clk(clk));  // open: clr
  Register #(.width(32)) register_15 (.D(WD), .en(and_25_out[1]), .Q(_2c), .clk(clk));  // open: clr
  Register #(.width(32)) register_16 (.D(WD), .en(and_29_out[1]), .Q(_6c), .clk(clk));  // open: clr
  Register #(.width(32)) register_17 (.D(WD), .en(and_1_out[2]), .Q(_3), .clk(clk));  // open: clr
  Register #(.width(32)) register_18 (.D(WD), .en(and_5_out[2]), .Q(_7), .clk(clk));  // open: clr
  Register #(.width(32)) register_19 (.D(WD), .en(and_9_out[2]), .Q(_3a), .clk(clk));  // open: clr
  Register #(.width(32)) register_20 (.D(WD), .en(and_13_out[2]), .Q(_7a), .clk(clk));  // open: clr
  Register #(.width(32)) register_21 (.D(WD), .en(and_17_out[2]), .Q(_3b), .clk(clk));  // open: clr
  Register #(.width(32)) register_22 (.D(WD), .en(and_21_out[2]), .Q(_7b), .clk(clk));  // open: clr
  Register #(.width(32)) register_23 (.D(WD), .en(and_25_out[2]), .Q(_3c), .clk(clk));  // open: clr
  Register #(.width(32)) register_24 (.D(WD), .en(and_29_out[2]), .Q(_7c), .clk(clk));  // open: clr
  Register #(.width(32)) register_25 (.D(WD), .en(and_1_out[3]), .Q(_4), .clk(clk));  // open: clr
  Register #(.width(32)) register_26 (.D(WD), .en(and_5_out[3]), .Q(_8), .clk(clk));  // open: clr
  Register #(.width(32)) register_27 (.D(WD), .en(and_9_out[3]), .Q(_4a), .clk(clk));  // open: clr
  Register #(.width(32)) register_28 (.D(WD), .en(and_13_out[3]), .Q(_8a), .clk(clk));  // open: clr
  Register #(.width(32)) register_29 (.D(WD), .en(and_17_out[3]), .Q(_4b), .clk(clk));  // open: clr
  Register #(.width(32)) register_30 (.D(WD), .en(and_21_out[3]), .Q(_8b), .clk(clk));  // open: clr
  Register #(.width(32)) register_31 (.D(WD), .en(and_25_out[3]), .Q(_4c), .clk(clk));  // open: clr
  Register #(.width(32)) register_32 (.D(WD), .en(and_29_out[3]), .Q(_8c), .clk(clk));  // open: clr
  Multiplexer #(.select(5), .width(32)) multiplexer_1 (
    .in0(_1), .in1(_2), .in2(_3), .in3(_4), .in4(_5), .in5(_6), .in6(_7), .in7(_8), .in8(_1a), .in9(_2a),
    .in10(_3a), .in11(_4a), .in12(_5a), .in13(_6a), .in14(_7a), .in15(_8a), .in16(_1b), .in17(_2b),
    .in18(_3b), .in19(_4b), .in20(_5b), .in21(_6b), .in22(_7b), .in23(_8b), .in24(_1c), .in25(_2c),
    .in26(_3c), .in27(_4c), .in28(_5c), .in29(_6c), .in30(_7c), .in31(_8c), .out(RD1), .sel(RA1));  // open: en
  Multiplexer #(.select(5), .width(32)) multiplexer_2 (
    .in0(_1), .in1(_2), .in2(_3), .in3(_4), .in4(_5), .in5(_6), .in6(_7), .in7(_8), .in8(_1a), .in9(_2a),
    .in10(_3a), .in11(_4a), .in12(_5a), .in13(_6a), .in14(_7a), .in15(_8a), .in16(_1b), .in17(_2b),
    .in18(_3b), .in19(_4b), .in20(_5b), .in21(_6b), .in22(_7b), .in23(_8b), .in24(_1c), .in25(_2c),
    .in26(_3c), .in27(_4c), .in28(_5c), .in29(_6c), .in30(_7c), .in31(_8c), .out(RD2), .sel(RA2));  // open: en
endmodule

module IFU (
  input  in_1,
  input  [31:0] in_2,
  input  in_3,
  output [31:0] Instr,
  output [31:0] out_5
);

  Register #(.width(32)) PC (.D(in_2), .Q(out_5), .clk(in_1), .clr(in_3));  // open: en
  ROM #(.addrWidth(5), .dataWidth(32)) rom_1 (.addr(out_5[6:2]), .data(Instr));  // open: sel
endmodule

module Splitter (
  input  [31:0] Instr,
  output [5:0] func,
  output [15:0] immediate,
  output [4:0] Rd,
  output [4:0] Rt,
  output [4:0] Rs,
  output [5:0] op
);


  assign func = Instr[5:0];
  assign immediate = Instr[15:0];
  assign op = Instr[31:26];
  assign Rd = Instr[15:11];
  assign Rs = Instr[25:21];
  assign Rt = Instr[20:16];
endmodule

module EXT (
  input  [1:0] Extop,
  input  [15:0] in_2,
  output [31:0] out_3
);

  wire [31:0] bit_extender_1_out, bit_extender_2_out;

  assign bit_extender_1_out = {{16{1'b0}}, in_2};  // Bit_Extender bit_extender_1
  assign bit_extender_2_out = {{16{in_2[15]}}, in_2};  // Bit_Extender bit_extender_2
  Multiplexer #(.select(2), .width(32)) multiplexer_1 (
    .in0(bit_extender_1_out), .in1(bit_extender_2_out), .in2({in_2, {16{1'b0}}}), .out(out_3), .sel(Extop));  // open: in3, en
endmodule
